// Logisim project control_logic.circ as structural Verilog: 1 circuit, main circuit control_logic
module control_logic (
  input  [31:0] inst,
  input  BrEq,
  input  BrLt,
  output PCSel,
  output RegWEn,
  output [2:0] ImmSel,
  output BrUn,
  output ASel,
  output BSel,
  output [3:0] ALUSel,
  output MemRW,
  output [1:0] WBSel,
  output CSRSel,
  output CSRWen,
  output lb,
  output lh,
  output sb,
  output sh
);

  wire add_r, addi, and_14_out, and_15_out, and_16_out, and_17_out, and_18_out, and_19_out, and_r, andi,
       auipc, beq, bge, bgeu, blt, bltu, bne, comparator_9_eq, comparator_10_eq, comparator_11_eq,
       comparator_12_eq, comparator_13_eq, comparator_14_eq, comparator_15_eq, comparator_16_eq,
       comparator_17_eq, comparator_18_eq, comparator_19_eq, comparator_20_eq, comparator_21_eq,
       comparator_22_eq, comparator_23_eq, csrw, demultiplexer_1_out1, demultiplexer_1_out5,
       demultiplexer_3_out0, demultiplexer_3_out1, demultiplexer_3_out5, I_type, I_type_L, jal, jalr, lui,
       lw, mul, mulh, mulhu, not_1_out, not_2_out, not_3_out, not_4_out, not_5_out, or_1_out, or_2_out,
       or_3_out, or_4_out, or_r, ori, priority_encoder_1_en_out, priority_encoder_2_en_out, R_type, S_type,
       SB_type, sll_r, slli, slt, slti, sra_r, srai, srl_r, srli, sub, sw, xor_r, xori;
  wire [3:1] rom_1_data;
  wire [4:0] priority_encoder_1_out, priority_encoder_2_out;
  wire [5:0] bit_extender_1_out, bit_extender_2_out, InstSel, multiplexer_1_out, multiplexer_2_out;

  Comparator #(.width(7)) comparator_1 (.a(inst[6:0]), .b(7'b0110011), .eq(R_type));  // open: gt, lt
  Comparator #(.width(7)) comparator_2 (.a(inst[6:0]), .b(7'b0000011), .eq(I_type_L));  // open: gt, lt
  Comparator #(.width(7)) comparator_3 (.a(inst[6:0]), .b(7'b0010011), .eq(I_type));  // open: gt, lt
  Comparator #(.width(7)) comparator_4 (.a(inst[6:0]), .b(7'b0100011), .eq(S_type));  // open: gt, lt
  Comparator #(.width(7)) comparator_5 (.a(inst[6:0]), .b(7'b1100011), .eq(SB_type));  // open: gt, lt
  Comparator #(.width(7)) comparator_6 (.a(inst[6:0]), .b(7'b0010111), .eq(auipc));  // open: gt, lt
  Comparator #(.width(7)) comparator_7 (.a(inst[6:0]), .b(7'b0110111), .eq(lui));  // open: gt, lt
  Comparator #(.width(7)) comparator_8 (.a(inst[6:0]), .b(7'b1101111), .eq(jal));  // open: gt, lt
  Comparator #(.width(7)) comparator_9 (.a(inst[6:0]), .b(7'b1100111), .eq(comparator_9_eq));  // open: gt, lt
  Comparator #(.width(3)) comparator_10 (.a(inst[14:12]), .b(3'b000), .eq(comparator_10_eq));  // open: gt, lt
  Comparator #(.width(7)) comparator_11 (.a(inst[6:0]), .b(7'b1110011), .eq(comparator_11_eq));  // open: gt, lt
  Comparator #(.width(3)) comparator_12 (.a(inst[14:12]), .b(3'b001), .eq(comparator_12_eq));  // open: gt, lt
  Comparator #(.width(3)) comparator_13 (.a(inst[14:12]), .b(3'b101), .eq(comparator_13_eq));  // open: gt, lt
  and and_1 (jalr, comparator_9_eq, comparator_10_eq);
  and and_2 (csrw, comparator_11_eq, comparator_12_eq);
  and and_3 (CSRSel, comparator_11_eq, comparator_13_eq);
  Demultiplexer #(.enable("false"), .select(3)) demultiplexer_1 (
    .out0(addi), .out1(demultiplexer_1_out1), .out2(slti), .out4(xori), .out5(demultiplexer_1_out5),
    .out6(ori), .out7(andi), .in(I_type), .sel(inst[14:12]));  // open: out3
  Demultiplexer #(.enable("false"), .select(3)) demultiplexer_2 (
    .out0(lb), .out1(lh), .out2(lw), .in(I_type_L), .sel(inst[14:12]));  // open: out3, out4, out5, out6, out7
  Demultiplexer #(.enable("false"), .select(3)) demultiplexer_3 (
    .out0(demultiplexer_3_out0), .out1(demultiplexer_3_out1), .out2(slt), .out3(mulhu), .out4(xor_r),
    .out5(demultiplexer_3_out5), .out6(or_r), .out7(and_r), .in(R_type), .sel(inst[14:12]));
  Demultiplexer #(.enable("false"), .select(3)) demultiplexer_4 (
    .out0(sb), .out1(sh), .out2(sw), .in(S_type), .sel(inst[14:12]));  // open: out3, out4, out5, out6, out7
  Comparator #(.width(7)) comparator_14 (.a({7{1'b0}}), .b(inst[31:25]), .eq(comparator_14_eq));  // open: gt, lt
  Comparator #(.width(7)) comparator_15 (.a({7{1'b0}}), .b(inst[31:25]), .eq(comparator_15_eq));  // open: gt, lt
  Comparator #(.width(7)) comparator_16 (.a(7'b0100000), .b(inst[31:25]), .eq(comparator_16_eq));  // open: gt, lt
  Comparator #(.width(7)) comparator_17 (.a({7{1'b0}}), .b(inst[31:25]), .eq(comparator_17_eq));  // open: gt, lt
  Comparator #(.width(7)) comparator_18 (.a(7'b0000001), .b(inst[31:25]), .eq(comparator_18_eq));  // open: gt, lt
  Comparator #(.width(7)) comparator_19 (.a(7'b0100000), .b(inst[31:25]), .eq(comparator_19_eq));  // open: gt, lt
  Comparator #(.width(7)) comparator_20 (.a({7{1'b0}}), .b(inst[31:25]), .eq(comparator_20_eq));  // open: gt, lt
  Comparator #(.width(7)) comparator_21 (.a(7'b0100000), .b(inst[31:25]), .eq(comparator_21_eq));  // open: gt, lt
  and and_4 (slli, demultiplexer_1_out1, comparator_14_eq);
  and and_5 (srli, demultiplexer_1_out5, comparator_15_eq);
  and and_6 (srai, demultiplexer_1_out5, comparator_16_eq);
  Demultiplexer #(.enable("false"), .select(3)) demultiplexer_5 (
    .out0(beq), .out1(bne), .out4(blt), .out5(bge), .out6(bltu), .out7(bgeu), .in(SB_type), .sel(inst[14:12]));  // open: out2, out3
  and and_7 (add_r, comparator_17_eq, demultiplexer_3_out0);
  and and_8 (mul, comparator_18_eq, demultiplexer_3_out0);
  and and_9 (sub, comparator_19_eq, demultiplexer_3_out0);
  and and_10 (sll_r, demultiplexer_3_out1, comparator_22_eq);
  Comparator #(.width(7)) comparator_22 (.a({7{1'b0}}), .b(inst[31:25]), .eq(comparator_22_eq));  // open: gt, lt
  and and_11 (mulh, demultiplexer_3_out1, comparator_23_eq);
  Comparator #(.width(7)) comparator_23 (.a(7'b0000001), .b(inst[31:25]), .eq(comparator_23_eq));  // open: gt, lt
  and and_12 (srl_r, demultiplexer_3_out5, comparator_20_eq);
  and and_13 (sra_r, demultiplexer_3_out5, comparator_21_eq);
  Comparator #(.width(7)) comparator_24 (.a(inst[6:0]), .b(7'b1110011), .eq(CSRWen));  // open: gt, lt
  Priority_Encoder #(.select(5)) priority_encoder_1 (
    .in0(add_r), .in1(mul), .in2(sub), .in3(sll_r), .in4(mulh), .in5(mulhu), .in6(slt), .in7(xor_r),
    .in8(srl_r), .in9(sra_r), .in10(or_r), .in11(and_r), .in12(lb), .in13(lh), .in14(lw), .in15(addi),
    .in16(slli), .in17(slti), .in18(xori), .in19(srli), .in20(srai), .in21(ori), .in22(andi), .in23(sb),
    .in24(sh), .in25(sw), .in26(beq), .in27(bne), .in28(blt), .in29(bge), .in30(bltu), .in31(bgeu),
    .out(priority_encoder_1_out), .en_out(priority_encoder_1_en_out));  // open: gs, en_in
  Priority_Encoder #(.select(5)) priority_encoder_2 (
    .in0(auipc), .in1(lui), .in2(jal), .in3(jalr), .in4(csrw), .in5(CSRSel), .out(priority_encoder_2_out),
    .en_out(priority_encoder_2_en_out));  // open: in6, in7, in8, in9, in10, in11, in12, in13, in14, in15, in16, in17, in18, in19, in20, in21, in22, in23, in24, in25, in26, in27, in28, in29, in30, in31, gs, en_in
  assign bit_extender_1_out = {{1{1'b0}}, priority_encoder_1_out};  // Bit_Extender bit_extender_1
  assign bit_extender_2_out = {{1{1'b1}}, priority_encoder_2_out};  // Bit_Extender bit_extender_2
  Multiplexer #(.enable("false"), .width(6)) multiplexer_1 (
    .in0(bit_extender_1_out), .in1({6{1'b0}}), .out(multiplexer_1_out), .sel(priority_encoder_1_en_out));
  Multiplexer #(.enable("false"), .width(6)) multiplexer_2 (
    .in0(bit_extender_2_out), .in1({6{1'b0}}), .out(multiplexer_2_out), .sel(priority_encoder_2_en_out));
  Adder #(.width(6)) adder_1 (.a(multiplexer_1_out), .b(multiplexer_2_out), .out(InstSel));  // open: cin, cout
  not not_1 (not_1_out, BrLt);
  not not_2 (not_2_out, BrEq);
  not not_3 (not_3_out, BrEq);
  or or_1 (or_1_out, BrEq, not_4_out);
  not not_4 (not_4_out, BrLt);
  not not_5 (not_5_out, BrEq);
  or or_2 (or_2_out, BrEq, not_1_out);
  ROM #(.addrWidth(6), .dataWidth(14)) rom_1 (
    .addr(InstSel), .data({WBSel, MemRW, ALUSel, BSel, ASel, BrUn, rom_1_data, RegWEn}));
  and and_14 (and_14_out, beq, BrEq);
  and and_15 (and_15_out, bne, not_2_out);
  and and_16 (and_16_out, blt, not_3_out, BrLt);
  and and_17 (and_17_out, bge, or_1_out);
  and and_18 (and_18_out, bltu, not_5_out, BrLt);
  and and_19 (and_19_out, bgeu, or_2_out);
  or or_3 (or_3_out, and_14_out, and_15_out, and_16_out, and_17_out, and_18_out, and_19_out);
  or or_4 (or_4_out, jal, jalr);
  or or_5 (PCSel, or_3_out, or_4_out);
  Multiplexer #(.enable("false"), .width(3)) multiplexer_3 (.in0(rom_1_data), .in1(3'b101), .out(ImmSel), .sel(CSRSel));

  // Other names for the same wires on the sheet: csrwi = CSRSel; ImmSelCSR = CSRSel; opcode[6:0] = inst[6:0];
  //   fun3[2:0] = inst[14:12]; fun7[6:0] = inst[31:25]

  // Notes on the sheet:
  //   INPUTS to your circuit
  //   DON'T CHANGE THE LOCATIONS OF THE INPUTS AND OUTPUTS!
  //   OUTPUT from your circuit
  //   contents of rom_1 (hex, n*v repeats v):
  //   1001 1501 1601 1301 1701 1581 1381 1181 1201 1281 1101 1081 841 841 841 1041 1341 13c1 11c1 1241
  //   12c1 1141 10c1 842 842 842 4*64 74 74 1067 1047 2069 2041
endmodule
